// Logisim project CPU.circ as structural Verilog: 1 circuit, main circuit main
module main (
  input  in_1
);

  wire clock_1_out, clock_2_out, CtrlA, MEM_CT, MEM_RW, not_1_out, not_2_out;
  wire [5:0] ALU;
  wire [7:0] ADDR, counter_1_q, MI_ADDR, RAMDATA_OUT, register_1_q;
  wire [22:0] rom_1_data;

  Clock clock_1 (.out(clock_1_out));
  Register register_1 (.D(MI_ADDR), .en(1'b1), .Q(register_1_q), .clk(clock_1_out), .clr(1'b0));
  Multiplexer #(.width(8), .enable("false")) multiplexer_1 (.in0(RAMDATA_OUT), .in1(ADDR), .out(MI_ADDR), .sel(CtrlA));
  ROM #(.dataWidth(32)) rom_1 (
    .addr(register_1_q), .data({ADDR, CtrlA, rom_1_data[22:21], ALU, MEM_CT, MEM_RW, rom_1_data[12:0]}),
    .sel(1'b1));
  Register register_2 ();  // open: D, en, Q, clk, clr
  Counter counter_1 (.load(1'b0), .count(not_1_out), .Q(counter_1_q), .clk(clock_2_out), .clr(in_1));  // open: D, carry
  not not_1 (not_1_out, MEM_CT);
  Clock clock_2 (.out(clock_2_out));
  // alu_main main_1: pin names not known; wires that end beside it: ALU[5], ALU[4], ALU[3], ALU[2], ALU[1], ALU[0]
  RAM #(.bus("separate")) ram_1 (
    .addr(counter_1_q), .data(RAMDATA_OUT), .sel(1'b1), .clk(clock_2_out), .ld(not_2_out), .clr(1'b0));  // open: din, str
  not not_2 (not_2_out, MEM_RW);

  // Notes on the sheet:
  //   contents of rom_1 (hex, n*v repeats v):
  //   0 0 0 1f8000 13*0 39e0000
endmodule
