// Logisim project Yasiru_CPU.circ as structural Verilog: 1 circuit, main circuit main
module main (
  input  in_1,
  output [31:0] out_2
);

  wire ADDR_MODE1, clock_1_out, clock_2_out, clock_3_out, clock_4_out, clock_5_out, decoder_1_out2,
       decoder_1_out3, decoder_1_out4, decoder_1_out5, decoder_1_out6, decoder_1_out7, decoder_2_out3,
       decoder_2_out4, decoder_2_out5, decoder_2_out6, decoder_2_out7, JMPC, MEM_FT, MEM_R, MEM_W, not_1_out,
       not_2_out, not_3_out;
  wire [2:0] A_BUS_CTRL, B_BUS_CTRL, multiplexer_3_out;
  wire [5:0] ALU, C_BUS_CTRL, C_BUS_CTRL_MI_1, multiplexer_2_out;
  wire [7:0] controlled_buffer_1_out, main_2_out, MI_ADDR, MI_NX_ADDR, OP_CODE, RAM_D_OUT, register_3_q,
       rom_1_data;
  wire [7:1] register_1_q;
  wire [15:0] counter_1_q;
  wire [22:21] register_2_q;
  wire [31:0] controlled_buffer_3_out, controlled_buffer_4_out, main_3_c, register_4_q, register_5_q,
       register_6_q, register_7_q, rom_2_data;

  Pull_Resistor pull_resistor_1 (.node(MI_ADDR));
  Pull_Resistor pull_resistor_2 (.node(MI_ADDR));
  ROM rom_1 (.addr(MI_ADDR), .data(rom_1_data), .sel(1'b1));
  Clock clock_1 (.out(clock_1_out));
  ROM #(.dataWidth(32)) rom_2 (.addr(MI_ADDR), .data(rom_2_data), .sel(1'b1));
  Clock clock_2 (.out(clock_2_out));
  Multiplexer #(.width(8), .enable("false")) multiplexer_1 (.in0(OP_CODE), .in1(MI_NX_ADDR), .out(MI_ADDR), .sel(JMPC));
  Register register_1 (.D(rom_1_data), .en(1'b1), .Q({register_1_q, ADDR_MODE1}), .clk(clock_1_out), .clr(1'b0));
  Register #(.width(32)) register_2 (
    .D(rom_2_data), .en(1'b1),
    .Q({MI_NX_ADDR, JMPC, register_2_q, ALU, MEM_FT, MEM_R, MEM_W, A_BUS_CTRL, B_BUS_CTRL, C_BUS_CTRL[0], C_BUS_CTRL[1], C_BUS_CTRL[2], C_BUS_CTRL[3], C_BUS_CTRL[4], C_BUS_CTRL[5]}),
    .clk(clock_2_out), .clr(1'b0));
  Clock clock_3 (.out(clock_3_out));
  Register register_3 (.D(RAM_D_OUT), .en(1'b1), .Q(register_3_q), .clk(clock_3_out), .clr(1'b0));
  assign controlled_buffer_1_out = MEM_FT ? register_3_q : 8'bz;  // Controlled_Buffer controlled_buffer_1
  assign OP_CODE = not_1_out ? register_3_q : 8'bz;  // Controlled_Buffer controlled_buffer_2
  not not_1 (not_1_out, MEM_R);
  Clock clock_4 (.out(clock_4_out));
  shift_reg_main main_1 (.DIN(controlled_buffer_1_out), .CLK(clock_4_out), .EN(1'b1), .CLR(1'b0), .DOUT(out_2));
  assign controlled_buffer_3_out = decoder_1_out7 ? out_2 : 32'bz;  // Controlled_Buffer controlled_buffer_3
  assign controlled_buffer_4_out = decoder_2_out7 ? out_2 : 32'bz;  // Controlled_Buffer controlled_buffer_4
  Multiplexer #(.width(6), .disabled(0), .enable("false")) multiplexer_2 (
    .in0(C_BUS_CTRL), .in1(C_BUS_CTRL_MI_1), .out(multiplexer_2_out), .sel(ADDR_MODE1));
  not not_2 (not_2_out, MEM_R);
  Counter #(.width(16), .max('hffff)) counter_1 (
    .load(multiplexer_2_out[3]), .D(main_3_c[15:0]), .count(not_2_out), .Q(counter_1_q), .clk(clock_5_out),
    .clr(in_1));  // open: carry
  Register #(.width(32)) register_4 (
    .D(main_3_c), .en(multiplexer_2_out[4]), .Q(register_4_q), .clk(clock_5_out), .clr(1'b0));
  Register #(.width(32)) register_5 (
    .D(main_3_c), .en(multiplexer_2_out[2]), .Q(register_5_q), .clk(clock_5_out), .clr(1'b0));
  Register #(.width(32)) register_6 (
    .D(main_3_c), .en(multiplexer_2_out[1]), .Q(register_6_q), .clk(clock_5_out), .clr(1'b0));
  Register #(.width(32)) register_7 (
    .D(main_3_c), .en(multiplexer_2_out[0]), .Q(register_7_q), .clk(clock_5_out), .clr(1'b0));
  Clock clock_5 (.out(clock_5_out));
  shitout_main main_2 (.IN(register_5_q), .CLK(clock_5_out), .CLR(multiplexer_2_out[3]), .OUT(main_2_out));
  assign controlled_buffer_3_out = decoder_1_out2 ? register_4_q : 32'bz;  // Controlled_Buffer controlled_buffer_5
  assign controlled_buffer_4_out = decoder_2_out3 ? register_4_q : 32'bz;  // Controlled_Buffer controlled_buffer_6
  assign controlled_buffer_3_out = decoder_1_out4 ? register_5_q : 32'bz;  // Controlled_Buffer controlled_buffer_7
  assign controlled_buffer_4_out = decoder_2_out4 ? register_5_q : 32'bz;  // Controlled_Buffer controlled_buffer_8
  assign controlled_buffer_3_out = decoder_1_out5 ? register_6_q : 32'bz;  // Controlled_Buffer controlled_buffer_9
  assign controlled_buffer_4_out = decoder_2_out5 ? register_6_q : 32'bz;  // Controlled_Buffer controlled_buffer_10
  assign controlled_buffer_3_out = decoder_1_out6 ? register_7_q : 32'bz;  // Controlled_Buffer controlled_buffer_11
  assign controlled_buffer_4_out = decoder_2_out6 ? register_7_q : 32'bz;  // Controlled_Buffer controlled_buffer_12
  RAM #(.addrWidth(16), .bus("separate")) ram_1 (
    .addr(counter_1_q), .din(main_2_out), .data(RAM_D_OUT), .str(MEM_W), .sel(1'b1), .clk(clock_5_out),
    .ld(not_3_out), .clr(1'b0));
  not not_3 (not_3_out, MEM_R);
  alu_main main_3 (.C(main_3_c), .A(controlled_buffer_4_out), .B(controlled_buffer_3_out), .ALU_CTRL(ALU));
  assign controlled_buffer_3_out[15:0] = decoder_1_out3 ? counter_1_q : 16'bz;  // Controlled_Buffer controlled_buffer_13
  Pull_Resistor pull_resistor_3 (.node(controlled_buffer_3_out[31:16]));
  Decoder #(.select(3), .disabled(0), .enable("false")) decoder_1 (
    .out2(decoder_1_out2), .out3(decoder_1_out3), .out4(decoder_1_out4), .out5(decoder_1_out5),
    .out6(decoder_1_out6), .out7(decoder_1_out7), .sel(multiplexer_3_out));  // open: out0, out1
  Decoder #(.select(3), .disabled(0), .enable("false")) decoder_2 (
    .out3(decoder_2_out3), .out4(decoder_2_out4), .out5(decoder_2_out5), .out6(decoder_2_out6),
    .out7(decoder_2_out7), .sel(A_BUS_CTRL));  // open: out0, out1, out2
  Decoder #(.select(3), .disabled(0), .enable("false")) decoder_3 (
    .out0(C_BUS_CTRL_MI_1[5]), .out1(C_BUS_CTRL_MI_1[4]), .out2(C_BUS_CTRL_MI_1[3]),
    .out3(C_BUS_CTRL_MI_1[2]), .out4(C_BUS_CTRL_MI_1[1]), .out5(C_BUS_CTRL_MI_1[0]), .sel(out_2[26:24]));  // open: out6, out7
  Multiplexer #(.width(3), .enable("false")) multiplexer_3 (
    .in0(B_BUS_CTRL), .in1(out_2[18:16]), .out(multiplexer_3_out), .sel(ADDR_MODE1));

  // Other names for the same wires on the sheet: A_BUS_CTRL_MI[2:0] = out_2[18:16]; C_BUS_CTRL_MI[2:0] = out_2[26:24]

  // Notes on the sheet:
  //   Micro Instuction Memory Module
  //   contents of rom_1 (hex, n*v repeats v):
  //   6*0 20 5*0 d0 0 60 0 60 0 a0 0 0 0 8 0 0 0 20 d0 4 4*0 44 15*0 1 1 1
  //   contents of rom_2 (hex, n*v repeats v):
  //   0 0 38c4000 4804000 5804000 6804000 70c0e20 0 9804000 a804000 b804000 c804000 a01d0 0 f1e0d60 0
  //   1f8d60 0 1f8ba0 0 0 0 178c4c08 18804000 19804000 1a804000 1b8c0e20 1c9b00d0 1d8c2c04 1e801000
  //   1f801000 20801000 21801000 221b2144 15*0 32804000 33804000 340a0000 0 36804000 37804000 388a40c2
  //   39804000 3a8c2e04 3b804000 3c804000 3d804000 3e804000 3f804000 408c0e20 411ca604 190*0 ff802000
  //   MI REG
  //   MI REG
  //   MBR
  //   Memory Data Fetch Unit
  //   FT REG
  //   1 to write
  //   0 to read
  //   1 to fetch
  //   C BUS
  //   PC
  //   GP1 REG
  //   MDR
  //   B REG
  //   A REG
  //   Random Access Memory Module
  //   A BUS
  //   B BUS
endmodule
