// Logisim project Yasiru_CPU_mem_fetch.circ as structural Verilog: 1 circuit, main circuit main
module main (
  input  in_1,
  output [31:0] out_2
);

  wire clock_1_out, clock_2_out, clock_3_out, main_2_p1, main_2_p8, not_1_out, not_2_out, not_3_out;
  wire [5:0] ALU;
  wire [7:0] controlled_buffer_2_out, MI_ADDR, MI_NX_ADDR, OP_CODE, RAM_D_OUT, register_1_q;
  wire [15:0] counter_1_q;

  Clock clock_1 (.out(clock_1_out));
  Multiplexer #(.width(8), .enable("false")) multiplexer_1 (.in0(OP_CODE), .in1(MI_NX_ADDR), .out(MI_ADDR), .sel(1'b0));
  assign OP_CODE = not_1_out ? register_1_q : 8'bz;  // Controlled_Buffer controlled_buffer_1
  Register register_1 (.D(RAM_D_OUT), .en(1'b1), .Q(register_1_q), .clk(clock_1_out), .clr(1'b0));
  assign controlled_buffer_2_out = 1'b0 ? register_1_q : 8'bz;  // Controlled_Buffer controlled_buffer_2
  Clock clock_2 (.out(clock_2_out));
  Pull_Resistor pull_resistor_1 (.node(OP_CODE));
  not not_1 (not_1_out, 1'b0);
  Pull_Resistor pull_resistor_2 (.node(controlled_buffer_2_out));
  shift_reg_main main_1 (.DIN(controlled_buffer_2_out), .CLK(clock_2_out), .EN(1'b1), .CLR(1'b0), .DOUT(out_2));
  not not_2 (not_2_out, 1'b0);
  Counter #(.width(16), .max('hffff)) counter_1 (
    .load(1'b0), .count(not_2_out), .Q(counter_1_q), .clk(clock_3_out), .clr(in_1));  // open: D, carry
  Clock clock_3 (.out(clock_3_out));
  RAM #(.addrWidth(16), .bus("separate")) ram_1 (
    .addr(counter_1_q), .data(RAM_D_OUT), .str(1'b0), .sel(1'b1), .clk(clock_3_out), .ld(not_3_out),
    .clr(1'b0));  // open: din
  not not_3 (not_3_out, 1'b0);
  // alu_main main_2: pin names not known; wires that end beside it: main_2_p1, ALU[5], ALU[4], ALU[3], ALU[2], ALU[1], ALU[0], main_2_p8

  // Other names for the same wires on the sheet: DATA_CONTRUCT[31:0] = out_2
endmodule
