// Logisim project alu.circ as structural Verilog: 1 circuit, main circuit main
module main (
  input  [31:0] A,
  input  [31:0] B,
  input  [5:0] ALU_CTRL,
  output [31:0] C
);

  wire [31:0] adder_1_out, and_1_out, controlled_buffer_1_out, controlled_buffer_2_out,
       controlled_buffer_3_out, not_1_out, or_1_out, xor_1_out;

  assign controlled_buffer_1_out = ALU_CTRL[1] ? {32{1'b1}} : 32'bz;  // Controlled_Buffer controlled_buffer_1
  assign controlled_buffer_2_out = ALU_CTRL[3] ? A : 32'bz;  // Controlled_Buffer controlled_buffer_2
  Pull_Resistor pull_resistor_1 (.node(controlled_buffer_2_out));
  assign controlled_buffer_3_out = ALU_CTRL[2] ? B : 32'bz;  // Controlled_Buffer controlled_buffer_3
  Pull_Resistor pull_resistor_2 (.node(controlled_buffer_3_out));
  Pull_Resistor pull_resistor_3 (.node(controlled_buffer_1_out));
  assign xor_1_out = controlled_buffer_1_out ^ controlled_buffer_2_out;  // XOR_Gate xor_1, 32 bits wide
  Adder #(.width(32)) adder_1 (
    .a(xor_1_out), .b(controlled_buffer_3_out), .out(adder_1_out), .cin(ALU_CTRL[0]));  // open: cout
  assign not_1_out = ~controlled_buffer_3_out;  // NOT_Gate not_1, 32 bits wide
  assign or_1_out = xor_1_out | controlled_buffer_3_out;  // OR_Gate or_1, 32 bits wide
  assign and_1_out = xor_1_out & controlled_buffer_3_out;  // AND_Gate and_1, 32 bits wide
  Multiplexer #(.select(2), .width(32), .disabled(0), .enable("false")) multiplexer_1 (
    .in0(and_1_out), .in1(or_1_out), .in2(not_1_out), .in3(adder_1_out), .out(C), .sel(ALU_CTRL[5:4]));
endmodule
