// Logisim project shift_reg.circ as structural Verilog: 1 circuit, main circuit main
module main (
  input  [7:0] DIN,
  input  CLK,
  input  EN,
  input  CLR,
  output [31:0] DOUT
);

  Register register_1 (.D(DIN), .en(EN), .Q(DOUT[31:24]), .clk(CLK), .clr(CLR));
  Register register_2 (.D(DOUT[31:24]), .en(EN), .Q(DOUT[23:16]), .clk(CLK), .clr(CLR));
  Register register_3 (.D(DOUT[23:16]), .en(EN), .Q(DOUT[15:8]), .clk(CLK), .clr(CLR));
  Register register_4 (.D(DOUT[15:8]), .en(EN), .Q(DOUT[7:0]), .clk(CLK), .clr(CLR));
endmodule
