// Logisim project shitout.circ as structural Verilog: 1 circuit, main circuit main
module main (
  input  [31:0] IN,
  input  CLK,
  input  CLR,
  output [7:0] OUT
);

  wire [1:0] counter_1_q;

  Counter #(.width(2), .max('h3)) counter_1 (
    .load(1'b0), .count(1'b1), .Q(counter_1_q), .clk(CLK), .clr(CLR));  // open: D, carry
  Multiplexer #(.select(2), .width(8), .enable("false")) multiplexer_1 (
    .in0(IN[7:0]), .in1(IN[15:8]), .in2(IN[23:16]), .in3(IN[31:24]), .out(OUT), .sel(counter_1_q));
endmodule
